// Digital circuit RV5-PROCESSOR.dig as structural Verilog
module RV5_PROCESSOR (
  input  clock,
  input  in_2,
  input  in_5,
  input  in_6,
  input  in_7,
  output out_3,
  output [1:0] out_4
);

  wire abstractcs_busy, abstractcs_wen, alu_mod, and_5_out, and_7_out, and_13_out, br_cond, branch_sel, clk,
       command_exec, command_reg_aarpostincrement, command_reg_arg0wen, command_reg_exec,
       command_reg_jumpprogbuf, command_reg_postexec, command_reg_regnoinvalid, command_reg_regwen,
       command_reg_sel, command_reg_transfer, command_reg_validtransferex, command_reg_write,
       command_unsuported_sel, command_wen, comparator_2_gt, comparator_3_eq, comparator_4_eq,
       comparator_6_lt, comparator_7_gt, comparator_8_eq, comparator_9_eq, comparator_10_gt,
       comparator_11_lt, csr_opclear, csr_opset, csr_opwrite, csr_useimm, csr_wen, d_ff_1_q, d_ff_2_q,
       d_ff_3_q, d_ff_4_q, dm_wen, dmcontrol_ackhavereset, dmcontrol_clrresethaltreq, dmcontrol_dmactive,
       dmcontrol_haltreq, dmcontrol_hartreset, dmcontrol_hasel, dmcontrol_ndmreset, dmcontrol_wen, dmi_ack_q,
       dmi_ren, dmi_req, dmi_wen, dmstatus_allhalted, dmstatus_allnonexistent, dmstatus_allresumeack,
       dmstatus_allrunning, dret_sel, ebreak_sel, ecall_sel, gdb_1_p1, gdb_1_p3, gdb_1_p4, gdb_1_p5, haltreq,
       I_imm_sel, jal_sel, jalr_sel, ld_signext, mret_sel, multiplexer_7_out, nor_1_out, not_2_out,
       not_4_out, not_5_out, not_6_out, or_3_out, or_4_out, or_6_out, or_9_out, or_10_out, or_12_out,
       or_13_out, ram_b, ram_h, ram_ren, ram_wen, reg_wen, register_1_q, S_imm_sel, SB_imm_sel, sbcs_wen,
       stopcond, U_imm_sel, UJ_imm_sel;
  wire [1:0] alu_a_sel, wb_sel;
  wire [1:1] rv5_tap_1_dmi_op;
  wire [2:0] abstractcs_cmderr, alu_op, and_8_out, command_reg_aarsize, funct3, multiplexer_4_out,
       multiplexer_6_out, not_3_out;
  wire [3:0] dmi_addr_lut_out;
  wire [4:0] command_reg_gprno, multiplexer_16_out, multiplexer_17_out, multiplexer_18_out,
       multiplexer_19_out, rd, rs1, rs2;
  wire [6:0] funct7, opcode, rv5_tap_1_dmi_addr;
  wire [7:0] command_cmdtype;
  wire [11:0] system_imm;
  wire [15:0] command_reg_regno;
  wire [15:5] sub_1_s;
  wire [19:0] dmcontrol_hartsel;
  wire [23:23] dmi_wdata;
  wire [30:2] dmcontrol_persistent;
  wire [30:3] dmcontrol_rdata;
  wire [31:0] addr_dm, alu_out, and_18_out, csr_out, dcsr, dm_wdata, dmi_rdata, dpc, imm_32, mem_out, mepc,
       mtvec, multiplexer_3_out, multiplexer_8_out, multiplexer_9_out, multiplexer_11_out,
       multiplexer_12_out, multiplexer_13_out, multiplexer_14_out, multiplexer_15_out, not_7_out, or_8_out,
       out_dm, ra, rb, rv5_memory_1_out_inst, rv5_pcu_1_pc;
  wire [31:2] nextpc;

  Register #(.Bits(32)) u_dmcontrol_persistent (
    .D({command_cmdtype, dmi_wdata[23], command_reg_aarsize, command_reg_aarpostincrement, command_reg_postexec, command_reg_transfer, command_reg_write, command_reg_regno}),
    .C(clk), .en(dmcontrol_wen),
    .Q({dmcontrol_haltreq, dmcontrol_persistent[30], dmcontrol_hartreset, dmcontrol_persistent[28:27], dmcontrol_hasel, dmcontrol_hartsel[9:0], dmcontrol_hartsel[19:10], dmcontrol_persistent[5:2], dmcontrol_ndmreset, dmcontrol_dmactive}));
  and and_1 (dmcontrol_clrresethaltreq, dmcontrol_wen, command_reg_regno[2]);
  and and_2 (dmcontrol_rdata[3], dmcontrol_wen, command_reg_regno[3]);
  and and_3 (dmcontrol_ackhavereset, dmcontrol_wen, command_cmdtype[4]);
  and and_4 (dmcontrol_rdata[30], dmcontrol_wen, command_cmdtype[6]);
  and and_5 (and_5_out, dmcontrol_rdata[30], dcsr[2]);
  D_FF d_ff_1 (.D(and_5_out), .C(clk), .Q(d_ff_1_q));  // open: nQ
  D_FF d_ff_2 (.D(d_ff_1_q), .C(clk), .Q(d_ff_2_q));  // open: nQ
  D_FF d_ff_3 (.D(d_ff_2_q), .C(clk), .Q(d_ff_3_q));  // open: nQ
  or or_1 (haltreq, dmcontrol_haltreq, d_ff_3_q);
  Register dmi_ack (.D(dmi_req), .C(clk), .en(1'b1), .Q(dmi_ack_q));
  not not_1 (dmstatus_allrunning, dmstatus_allhalted);
  Comparator #(.Bits(20)) comparator_1 (
    .a(dmcontrol_hartsel), .b({20{1'b0}}), .gt(dmstatus_allnonexistent));  // open: eq, lt
  RS_FF rs_ff_1 (.S(dmcontrol_rdata[30]), .C(clk), .R(dmcontrol_haltreq), .Q(dmstatus_allresumeack));  // open: nQ
  // Gdb gdb_1: pin names not known; wires that end beside it: gdb_1_p1, clk, gdb_1_p3, gdb_1_p4, gdb_1_p5
  RV5_TAP rv5_tap_1 (
    .TCK(gdb_1_p3), .RESET(in_2), .TDI(gdb_1_p5), .TMS(gdb_1_p4), .DMI_ACK(dmi_ack_q), .DMI_RDATA(dmi_rdata),
    .DMI_STATUS(2'b00), .TDO(gdb_1_p1), .DMI_REQ(dmi_req), .DMI_ADDR(rv5_tap_1_dmi_addr),
    .DMI_WDATA({command_cmdtype, dmi_wdata[23], command_reg_aarsize, command_reg_aarpostincrement, command_reg_postexec, command_reg_transfer, command_reg_write, command_reg_regno}),
    .DMI_OP({rv5_tap_1_dmi_op[1], dmi_ren}), .E_DMI_BUSY(out_3), .E_STICKY_ERR(out_4));  // open: E_DMISTAT
  not not_2 (not_2_out, abstractcs_busy);
  and and_6 (dmi_wen, dmi_req, not_2_out, rv5_tap_1_dmi_op[1]);
  LookUpTable #(.Bits(4)) dmi_addr_lut (
    .in0(rv5_tap_1_dmi_addr[0]), .in1(rv5_tap_1_dmi_addr[1]), .in2(rv5_tap_1_dmi_addr[2]),
    .in3(rv5_tap_1_dmi_addr[3]), .in4(rv5_tap_1_dmi_addr[4]), .in5(rv5_tap_1_dmi_addr[5]),
    .in6(rv5_tap_1_dmi_addr[6]), .out(dmi_addr_lut_out));
  Demultiplexer #(.Selector_Bits(4)) demultiplexer_1 (
    .sel(dmi_addr_lut_out), .in(dmi_wen), .out_2(dmcontrol_wen), .out_5(abstractcs_wen), .out_6(command_wen),
    .out_15(sbcs_wen));  // open: out_0, out_1, out_3, out_4, out_7, out_8, out_9, out_10, out_11, out_12, out_13, out_14
  or or_2 (dm_wen, dmi_wen, command_reg_arg0wen);
  Multiplexer #(.Bits(32)) multiplexer_1 (
    .sel(command_reg_arg0wen),
    .in_0({command_cmdtype, dmi_wdata[23], command_reg_aarsize, command_reg_aarpostincrement, command_reg_postexec, command_reg_transfer, command_reg_write, command_reg_regno}),
    .in_1(ra), .out(dm_wdata));
  and and_7 (and_7_out, command_reg_regnoinvalid, command_reg_transfer);
  Multiplexer #(.Selector_Bits(4), .Bits(32)) multiplexer_2 (
    .sel(dmi_addr_lut_out), .in_0({32{1'b0}}), .in_1(out_dm),
    .in_2({dmcontrol_haltreq, dmcontrol_rdata[30], dmcontrol_hartreset, dmcontrol_ackhavereset, 1'b0, dmcontrol_hasel, dmcontrol_hartsel[9:0], dmcontrol_hartsel[19:10], 2'b00, dmcontrol_rdata[3], dmcontrol_clrresethaltreq, dmcontrol_ndmreset, dmcontrol_dmactive}),
    .in_3({{14{1'b0}}, {2{dmstatus_allresumeack}}, {2{dmstatus_allnonexistent}}, 2'b00, {2{dmstatus_allrunning}}, {2{dmstatus_allhalted}}, 8'h82}),
    .in_4(32'h111024), .in_5({19'h4000, abstractcs_busy, 1'b0, abstractcs_cmderr, 8'h1}), .in_6({32{1'b0}}),
    .in_7(out_dm), .in_8(out_dm), .in_9(out_dm), .in_10(out_dm), .in_11(out_dm), .in_12(out_dm),
    .in_13(out_dm), .in_14(out_dm), .in_15(32'h20000000), .out(dmi_rdata));
  Comparator #(.Bits(3)) comparator_2 (.a(command_reg_aarsize), .b(3'b010), .gt(comparator_2_gt));  // open: eq, lt
  Multiplexer #(.Selector_Bits(4), .Bits(32)) multiplexer_3 (
    .sel(dmi_addr_lut_out), .in_0({32{1'b0}}), .in_1(32'h1024), .in_2({32{1'b0}}), .in_3({32{1'b0}}),
    .in_4({32{1'b0}}), .in_5({32{1'b0}}), .in_6({32{1'b0}}), .in_7(32'h1004), .in_8(32'h1008),
    .in_9(32'h100c), .in_10(32'h1010), .in_11(32'h1014), .in_12(32'h1018), .in_13(32'h101c),
    .in_14(32'h1020), .in_15({32{1'b0}}), .out(multiplexer_3_out));
  or or_3 (or_3_out, command_unsuported_sel, comparator_2_gt, and_7_out, command_reg_aarpostincrement);
  Multiplexer #(.Bits(3)) multiplexer_4 (.sel(or_3_out), .in_0(3'b000), .in_1(3'b010), .out(multiplexer_4_out));
  Multiplexer #(.Bits(32)) multiplexer_5 (
    .sel(command_reg_arg0wen), .in_0(multiplexer_3_out), .in_1(32'h1024), .out(addr_dm));
  assign and_8_out = not_3_out & abstractcs_cmderr;  // And and_8, 3 bits wide
  assign not_3_out = ~command_reg_regno[10:8];  // Not not_3, 3 bits wide
  Multiplexer #(.Bits(3)) multiplexer_6 (
    .sel(command_reg_exec), .in_0(and_8_out), .in_1(multiplexer_4_out), .out(multiplexer_6_out));
  or or_4 (or_4_out, abstractcs_wen, command_exec);
  Register #(.Bits(3)) u_abstractcs_cmderr (.D(multiplexer_6_out), .C(clk), .en(or_4_out), .Q(abstractcs_cmderr));
  Comparator #(.Bits(12)) comparator_3 (.a(12'h7b0), .b(system_imm), .eq(comparator_3_eq));  // open: gt, lt
  Comparator #(.Bits(32)) comparator_4 (.a(addr_dm), .b(32'h1024), .eq(comparator_4_eq));  // open: gt, lt
  nor nor_1 (nor_1_out, abstractcs_cmderr[0], abstractcs_cmderr[1], abstractcs_cmderr[2]);
  Comparator #(.Bits(8)) comparator_5 (
    .a(command_cmdtype), .b({8{1'b0}}), .gt(command_unsuported_sel), .eq(command_reg_sel));  // open: lt
  and and_9 (command_reg_exec, command_exec, command_reg_sel);
  Comparator #(.Bits(16)) comparator_6 (.a(command_reg_regno), .b(16'h1000), .lt(comparator_6_lt));  // open: gt, eq
  Comparator #(.Bits(16)) comparator_7 (.a(command_reg_regno), .b(16'h101f), .gt(comparator_7_gt));  // open: eq, lt
  // And and_10 has open pins: In_1=comparator_3_eq, In_2=csr_wen, out=open
  // And and_11 has open pins: In_1=comparator_4_eq, In_2=dm_wen, In_3=command_reg_regno[2], out=open
  and and_12 (command_exec, command_wen, nor_1_out);
  or or_5 (command_reg_regnoinvalid, comparator_6_lt, comparator_7_gt);
  D_FF d_ff_4 (.D(in_7), .C(clk), .Q(d_ff_4_q));  // open: nQ
  not not_4 (not_4_out, d_ff_4_q);
  and and_13 (and_13_out, not_4_out, in_7);
  Multiplexer multiplexer_7 (.sel(in_7), .in_0(1'b0), .in_1(1'b0), .out(multiplexer_7_out));
  or or_6 (or_6_out, 1'b0, and_13_out);
  not not_5 (not_5_out, command_reg_regnoinvalid);
  and and_14 (command_reg_arg0wen, not_6_out, command_reg_validtransferex);
  not not_6 (not_6_out, command_reg_write);
  and and_15 (command_reg_regwen, command_reg_write, command_reg_validtransferex);
  Sub #(.Bits(16)) sub_1 (
    .a(command_reg_regno), .b(16'h1000), .c_i(1'b0), .s({sub_1_s, command_reg_gprno}));  // open: c_o
  and and_16 (command_reg_jumpprogbuf, command_reg_postexec, command_reg_exec);
  and and_17 (command_reg_validtransferex, command_reg_exec, command_reg_transfer, not_5_out);
  Register register_1 (.D(multiplexer_7_out), .C(clk), .en(or_6_out), .Q(register_1_q));
  or or_7 (stopcond, 1'b0, register_1_q);
  Multiplexer #(.Bits(32)) multiplexer_8 (
    .sel(csr_useimm), .in_0(ra), .in_1({{27{1'b0}}, rs1}), .out(multiplexer_8_out));
  assign not_7_out = ~multiplexer_8_out;  // Not not_7, 32 bits wide
  assign and_18_out = not_7_out & csr_out;  // And and_18, 32 bits wide
  assign or_8_out = multiplexer_8_out | csr_out;  // Or or_8, 32 bits wide
  Multiplexer #(.Bits(32)) multiplexer_9 (
    .sel(csr_opclear), .in_0(multiplexer_8_out), .in_1(and_18_out), .out(multiplexer_9_out));
  Multiplexer multiplexer_10 (.sel(or_9_out), .in_0(clock), .in_1(in_5), .out(clk));
  RV5_PCU rv5_pcu_1 (
    .IMM_32(imm_32), .CLK(clk), .IS_BRANCH(branch_sel), .IS_JAL(jal_sel), .IS_JALR(jalr_sel),
    .COND_MET(br_cond), .ALU_OUT(alu_out), .IS_ECALL(ecall_sel), .MTVEC(mtvec), .MEPC(mepc),
    .IS_MRET(mret_sel), .IS_EBREAK(ebreak_sel), .IS_DEBUG(dmstatus_allhalted), .DCSR(dcsr), .DPC(dpc),
    .IS_DRET(dret_sel), .HALTREQ(haltreq), .JUMPPROGBUF(command_reg_jumpprogbuf),
    .RESUMEREQ(dmcontrol_rdata[30]), .PC(rv5_pcu_1_pc));
  Multiplexer #(.Bits(32)) multiplexer_11 (
    .sel(csr_opset), .in_0(multiplexer_9_out), .in_1(or_8_out), .out(multiplexer_11_out));
  or or_9 (or_9_out, in_6, stopcond);
  Comparator #(.Bits(32)) comparator_8 (.a(rv5_pcu_1_pc), .b(32'h190), .eq(comparator_8_eq));  // open: gt, lt
  Comparator #(.Bits(32)) comparator_9 (.a(rv5_pcu_1_pc), .b(32'h194), .eq(comparator_9_eq));  // open: gt, lt
  Comparator #(.Bits(32)) comparator_10 (.a(rv5_pcu_1_pc), .b(32'h1003), .gt(comparator_10_gt));  // open: eq, lt
  Comparator #(.Bits(32)) comparator_11 (.a(rv5_pcu_1_pc), .b(32'h1021), .lt(comparator_11_lt));  // open: gt, eq
  RV5_IMM rv5_imm_1 (
    .UJ_imm_sel(UJ_imm_sel), .I_imm_sel(I_imm_sel), .SB_imm_sel(SB_imm_sel), .S_imm_sel(S_imm_sel),
    .U_imm_sel(U_imm_sel), .INSTR_32(rv5_memory_1_out_inst), .imm(imm_32));
  Add #(.Bits(30)) add_1 (.a(rv5_pcu_1_pc[31:2]), .b({30{1'b0}}), .c_i(1'b1), .s(nextpc));  // open: c_o
  RV5_CSR rv5_csr_1 (
    .clk(clk), .addr(system_imm), .w_data(multiplexer_11_out), .wen(csr_wen), .pc_in(rv5_pcu_1_pc),
    .ecall_sel(ecall_sel), .mret_sel(mret_sel), .ebreak_sel(ebreak_sel), .is_debug(dmstatus_allhalted),
    .haltreq(haltreq), .R_DATA(csr_out), .MTVEC_OUT(mtvec), .MEPC_OUT(mepc), .DCSR_OUT(dcsr), .DPC_OUT(dpc));
  or or_10 (or_10_out, comparator_8_eq, comparator_9_eq);
  and and_19 (abstractcs_busy, comparator_10_gt, comparator_11_lt);
  or or_11 (dmstatus_allhalted, or_10_out, abstractcs_busy);
  RV5_INSTR_DECODE rv5_instr_decode_1 (
    .instr(rv5_memory_1_out_inst), .funct7(funct7), .rs2(rs2), .rs1(rs1), .funct3(funct3), .rd(rd),
    .opcode(opcode), .UJ_imm_sel(UJ_imm_sel), .U_imm_sel(U_imm_sel), .S_imm_sel(S_imm_sel),
    .SB_imm_sel(SB_imm_sel), .I_imm_sel(I_imm_sel), .alu_mod(alu_mod), .ram_wen(ram_wen), .wb_sel(wb_sel),
    .ram_ren(ram_ren), .ecall_sel(ecall_sel), .alu_op(alu_op), .ram_b(ram_b), .ram_h(ram_h),
    .reg_wen(reg_wen), .branch_sel(branch_sel), .jal_sel(jal_sel), .jalr_sel(jalr_sel),
    .alu_a_sel(alu_a_sel), .ld_signext(ld_signext), .csr_wen(csr_wen), .mret_sel(mret_sel),
    .system_imm(system_imm), .ebreak_sel(ebreak_sel), .dret_sel(dret_sel), .csr_opwrite(csr_opwrite),
    .csr_opset(csr_opset), .csr_opclear(csr_opclear), .csr_useimm(csr_useimm));
  RV5_MEMORY rv5_memory_1 (
    .addr(alu_out), .wdata(rb), .wen(ram_wen), .ren(ram_ren), .clk(clk), .\byte (ram_b), .half(ram_h),
    .signext(ld_signext), .addr_inst(rv5_pcu_1_pc), .addr_dm(addr_dm), .wen_dm(dm_wen), .wdata_dm(dm_wdata),
    .out(mem_out), .out_inst(rv5_memory_1_out_inst), .out_dm(out_dm));  // open: d0O
  Multiplexer #(.Selector_Bits(2), .Bits(32)) multiplexer_12 (
    .sel(alu_a_sel), .in_0(ra), .in_1(rv5_pcu_1_pc), .in_2({32{1'b0}}), .in_3({32{1'b0}}),
    .out(multiplexer_12_out));
  Multiplexer #(.Bits(32)) multiplexer_13 (.sel(or_12_out), .in_0(rb), .in_1(imm_32), .out(multiplexer_13_out));
  or or_12 (or_12_out, I_imm_sel, S_imm_sel, U_imm_sel);
  RV5_ALU rv5_alu_1 (
    .OP(alu_op), .Y(alu_out), .A(multiplexer_12_out), .B(multiplexer_13_out), .BR(br_cond), .MOD(alu_mod));
  Multiplexer #(.Selector_Bits(2), .Bits(32)) multiplexer_14 (
    .sel(wb_sel), .in_0(alu_out), .in_1({nextpc, 2'b00}), .in_2(mem_out), .in_3(csr_out),
    .out(multiplexer_14_out));
  Multiplexer #(.Bits(32)) multiplexer_15 (
    .sel(command_reg_exec), .in_0(multiplexer_14_out), .in_1(out_dm), .out(multiplexer_15_out));
  Multiplexer #(.Bits(5)) multiplexer_16 (.sel(ecall_sel), .in_0(rs1), .in_1(5'b01010), .out(multiplexer_16_out));
  Multiplexer #(.Bits(5)) multiplexer_17 (
    .sel(command_reg_exec), .in_0(multiplexer_16_out), .in_1(command_reg_gprno), .out(multiplexer_17_out));
  Multiplexer #(.Bits(5)) multiplexer_18 (.sel(ecall_sel), .in_0(rs2), .in_1(5'b10001), .out(multiplexer_18_out));
  or or_13 (or_13_out, reg_wen, command_reg_regwen);
  Multiplexer #(.Bits(5)) multiplexer_19 (
    .sel(command_reg_exec), .in_0(rd), .in_1(command_reg_gprno), .out(multiplexer_19_out));
  RV5_GPR rv5_gpr_1 (
    .RS1(multiplexer_17_out), .RS2(multiplexer_18_out), .D_in(multiplexer_15_out), .clk(clk),
    .WEN(or_13_out), .RD(multiplexer_19_out), .RA(ra), .RB(rb));  // open: RD0

  // Other names for the same wires on the sheet: abstractcs_rdata (some bits) = {abstractcs_busy, abstractcs_cmderr};
  //   dmcontrol_rdata (some bits) = {dmcontrol_haltreq, dmcontrol_hartreset, dmcontrol_ackhavereset, dmcontrol_hasel, dmcontrol_hartsel[9:0], dmcontrol_hartsel[19:10], dmcontrol_clrresethaltreq, dmcontrol_ndmreset, dmcontrol_dmactive};
  //   dmcontrol_persistent (some bits) = {dmcontrol_haltreq, dmcontrol_hartreset, dmcontrol_hasel, dmcontrol_hartsel[9:0], dmcontrol_hartsel[19:10], dmcontrol_ndmreset, dmcontrol_dmactive};
  //   dmcontrol_hartselhi[9:0] = dmcontrol_hartsel[19:10]; dmcontrol_hartsello[9:0] = dmcontrol_hartsel[9:0];
  //   dmcontrol_resumereq = dmcontrol_rdata[30]; dmcontrol_setresethaltreq = dmcontrol_rdata[3];
  //   dmi_wdata (some bits) = {command_cmdtype, command_reg_aarsize, command_reg_aarpostincrement, command_reg_postexec, command_reg_transfer, command_reg_write, command_reg_regno};
  //   dmstatus_anynonexistent = dmstatus_allnonexistent;
  //   dmstatus_rdata (some bits) = {{2{dmstatus_allresumeack}}, {2{dmstatus_allnonexistent}}, {2{dmstatus_allrunning}}, {2{dmstatus_allhalted}}};
  //   dmstatus_anyresumeack = dmstatus_allresumeack; dmstatus_anyrunning = dmstatus_allrunning;
  //   in_progbuf = abstractcs_busy; dmstatus_anyhalted = dmstatus_allhalted; is_debug = dmstatus_allhalted

  // Notes on the sheet:
  //   clock: Hz: 2147483647
  //   in_5: default 1
  //   Debug module registers:
  //   dmcontrol
  //   We store any fields that need to be
  //   persistent in a register:
  //   Every RW field can be directly
  //   extracted for use from the
  //   persistent register:
  //   W1 fields should only be high
  //   for the clock cycle that they're written:
  //   It's useful to have each field separate
  //   for implementing their functionality,
  //   but let's also pack them up
  //   so that the debugger can read them:
  //   (And for convenience, let's 
  //   also expose this:)
  //   sbcs
  //   We don't support system bus
  //   access, so we can treat this entire
  //   register as effectively read-only:
  //   Todo:
  //   **MOVE AROUND MEM TO MAKE DATA0
  //      SOMETHING THAT CAN BE ADDRESSED
  //      BY HARTINFO**
  //   Access register impl
  //   dcsr cause field
  //   look into other unimplemented fields
  //   dmstatus
  //   Every field in mstatus is read-only.
  //   Determine each field's value:
  //   Pack them up so the debugger
  //   can read them:
  //   contents of dmi_addr_lut (hex, n*v repeats v):
  //   4*0,1,11*0,2,3,4,0,0,0,5,6,8*0,7,8,9,a,b,c,d,e,16*0,f
  //   abstractcs
  //   Determine each field's value:
  //   (especially cmderr...)
  //   We only support the access register
  //   command. This is because it 
  //   can execute arbitrary code in
  //   progbuf, allowing us to do 
  //   everything we want.
  //   hartinfo
  //   Debug stuff
  //   command
  //   This is a write-only register. 
  //   We choose to process it entirely on the same cycle it is written.
  //   I should mention that we only implement the access register
  //   command. This is because it contains functionality for arbitrary
  //   code execution, which allows us to do everything else.
  //   Extract all fields:
  //   Figure out if we should be executing
  //   the command:
  //   Split out cmdtype to selectors:
  //   Determine if we need to execute a register access
  //   command:
  //   Figure out if regno is invalid:
  //   Determine if a valid transfer is to be executed:
  //   Will we end up reading a register?
  //   Let's see:
  //   What about writing?
  //   If we end up reading or writing a
  //   register, we'll need its number in
  //   the standard format:
  //   And finally figure out if we need to
  //   jump to the progbuf:
  //   For now, address range check is
  //   the most robust way to know if
  //   we're in debug mode.
  //   Might change so debug ROM length
  //   is variable, but for now I KNOW this
  //   works.
  //   Here we are trying to make this circuit hierarchical
  //       RV5-REGS contains register bank related hw.
  //       RV5-ALU contains ALU related hw
  //       RV5-INSTR-DECODE contains Instruction Reg, and all needed decodes
  //             decoder for immediate sel
  //       RV5-IMM is a combinatorial that extracts the needed immediates, 
  //              and provides the sign-extended 32-bit value thru a MUX.
  //       RV5-PCU needs some fixes.
  //              increments the PC and allows Jumps, and provides next PC for JAL save of PC.
  //   See examples in Digital in particular processors as to how 
  //   to do this.  
  //   TODO: 
  //   1st. Add a test to each element in the hierarchy.
  //   2nd Resize boxes with appropriate SVG for readable packages w. appropriate signals.
  //   We need to:
  //       RV5-INSTR-DECODE: Decodes the instruction set and provides control signals, and FMT
  //            decode for immediate select has been completed.
  //       Implement:
  //            RV5-LOAD-STORE: Provides Load and Store
  //            RV5-MEMORY: Include ROM and RAM.
  //            RV5-IO: Provides a mean to read a program, communicate with a terminal (keyboard/display)
  //            Create a ROM/RAM  bootstrap
  //                 that loads a program.
  //   Note: Assembler test programs can be found at:   
  //      https://github.com/riscv-software-src/riscv-tests
  //   PCU (Program Control Unit, 
  //   PC = PC + 4, or PC = PC += SBimm32
  //   or PC = ALU out or PC += sgn_ext-imm32
  //   for FMT U, and UJ
  //   Need to figure out a way to load memory
  //   with instructions, ideally from RARS.
  //   Check out how MARS does it for MIPS.
  //   NEXT, NEED LOAD AND STORE,
  //   Address comes from ALU output
  //   which goes to memory via see-thru latch
  //    latch,which goes out to memory for 
  //   loading and storing.  reads 32-word
  //   and stores in rd.   Need to figure out a good
  //   approach to read and write to memory 
  //   with Digital and load it at start up.
  //   We need to arbitrate use of memory 
  //   between load/store and fetching instruction.
  //   RV5-DECODER:
  //      decodes: opcode, funct3, funct7
  //      generates: 
  //           # FMT - DO I NEED IT HERE?
  //           # imm_sel,  DONE ALREADY
  //           wen, 
  //           sub/add, 
  //           func_sel
endmodule
